// Logisim project sap2_main.circ as structural Verilog: 1 circuit, main circuit main
module main (
  input  in_1,
  input  in_2,
  input  in_3,
  input  in_4,
  input  in_5,
  input  in_6,
  input  [2:0] in_7,
  input  in_8,
  input  in_9,
  input  in_10,
  input  in_11,
  input  in_12,
  input  in_13,
  input  in_14,
  input  in_15,
  input  in_16,
  input  in_17,
  input  in_18,
  input  in_19,
  input  in_20,
  input  in_21,
  input  in_22,
  input  in_23,
  input  in_24,
  input  in_25,
  input  in_26,
  input  in_27,
  output [15:0] out_28,
  output [15:0] out_29,
  output [15:0] out_30
);

  wire arithmetic_logic_unit_1_carry, arithmetic_logic_unit_1_sign, CLK, nor_1_out;
  wire [7:0] ram_1_dout, register_8_1_q1, register_8_2_o1, register_8_3_o1;
  wire [15:0] register_16_1_q1;

  Clock clock_1 (.out(CLK));
  RAM #(.addrWidth(16), .asyncread("true")) ram_1 (
    .addr(register_16_1_q1), .we(in_13), .oe(in_14), .clk(CLK), .din(out_28[7:0]), .dout(ram_1_dout));
  pc pc_1 (.EN(in_3), .LOAD(in_4), .COUNT(in_5), .CLK(CLK), .D_in(out_28), .Q_out(out_28), .O_out(out_29));
  register_16 register_16_1 (
    .D1(out_28[0]), .D2(out_28[1]), .D3(out_28[2]), .D4(out_28[3]), .D5(out_28[4]), .D6(out_28[5]),
    .D7(out_28[6]), .D8(out_28[7]), .D9(out_28[8]), .D10(out_28[9]), .D11(out_28[10]), .D12(out_28[11]),
    .D13(out_28[12]), .D14(out_28[13]), .D15(out_28[14]), .D16(out_28[15]), .LOAD(in_9), .CLK(CLK),
    .EN(in_10), .O1(out_30[0]), .O2(out_30[1]), .O3(out_30[2]), .O4(out_30[3]), .O5(out_30[4]),
    .O6(out_30[5]), .O7(out_30[6]), .O8(out_30[7]), .O9(out_30[8]), .O10(out_30[9]), .O11(out_30[10]),
    .O12(out_30[11]), .O13(out_30[12]), .O14(out_30[13]), .O15(out_30[14]), .O16(out_30[15]),
    .Q1(register_16_1_q1[0]), .Q2(register_16_1_q1[1]), .Q3(register_16_1_q1[2]), .Q4(register_16_1_q1[3]),
    .Q5(register_16_1_q1[4]), .Q6(register_16_1_q1[5]), .Q7(register_16_1_q1[6]), .Q8(register_16_1_q1[7]),
    .Q9(register_16_1_q1[8]), .Q10(register_16_1_q1[9]), .Q11(register_16_1_q1[10]),
    .Q12(register_16_1_q1[11]), .Q13(register_16_1_q1[12]), .Q14(register_16_1_q1[13]),
    .Q15(register_16_1_q1[14]), .Q16(register_16_1_q1[15]));
  register_8 register_8_1 (
    .D1(ram_1_dout[0]), .D2(ram_1_dout[1]), .D3(ram_1_dout[2]), .D4(ram_1_dout[3]), .D5(ram_1_dout[4]),
    .D6(ram_1_dout[5]), .D7(ram_1_dout[6]), .D8(ram_1_dout[7]), .LOAD(in_15), .CLK(CLK), .EN(in_16),
    .Q1(register_8_1_q1[0]), .Q2(register_8_1_q1[1]), .Q3(register_8_1_q1[2]), .Q4(register_8_1_q1[3]),
    .Q5(register_8_1_q1[4]), .Q6(register_8_1_q1[5]), .Q7(register_8_1_q1[6]), .Q8(register_8_1_q1[7]));  // open: O1, O2, O3, O4, O5, O6, O7, O8
  Demultiplexer #(.tristate("true"), .width(8)) demultiplexer_1 (
    .out0(out_28[7:0]), .out1(out_28[15:8]), .in(register_8_1_q1), .sel(in_17));
  register_z16bits register_z16bits_1 (
    .D1(out_28[0]), .D2(out_28[1]), .D3(out_28[2]), .D4(out_28[3]), .D5(out_28[4]), .D6(out_28[5]),
    .D7(out_28[6]), .D8(out_28[7]), .D9(out_28[8]), .D10(out_28[9]), .D11(out_28[10]), .D12(out_28[11]),
    .D13(out_28[12]), .D14(out_28[13]), .D15(out_28[14]), .D16(out_28[15]), .CLK(CLK), .LOAD1(in_20),
    .LOAD2(in_21), .EN1(in_22), .EN2(in_23), .Q1(out_28[0]), .Q2(out_28[1]), .Q3(out_28[2]), .Q4(out_28[3]),
    .Q5(out_28[4]), .Q6(out_28[5]), .Q7(out_28[6]), .Q8(out_28[7]), .Q9(out_28[8]), .Q10(out_28[9]),
    .Q11(out_28[10]), .Q12(out_28[11]), .Q13(out_28[12]), .Q14(out_28[13]), .Q15(out_28[14]), .Q16(out_28[15]));  // open: O1, O2, O3, O4, O5, O6, O7, O8, O9, O10, O11, O12, O13, O14, O15, O16
  register_8 register_8_2 (
    .D1(out_28[0]), .D2(out_28[1]), .D3(out_28[2]), .D4(out_28[3]), .D5(out_28[4]), .D6(out_28[5]),
    .D7(out_28[6]), .D8(out_28[7]), .LOAD(in_1), .CLK(CLK), .EN(in_2), .O1(register_8_2_o1[0]),
    .O2(register_8_2_o1[1]), .O3(register_8_2_o1[2]), .O4(register_8_2_o1[3]), .O5(register_8_2_o1[4]),
    .O6(register_8_2_o1[5]), .O7(register_8_2_o1[6]), .O8(register_8_2_o1[7]), .Q1(out_28[0]),
    .Q2(out_28[1]), .Q3(out_28[2]), .Q4(out_28[3]), .Q5(out_28[4]), .Q6(out_28[5]), .Q7(out_28[6]),
    .Q8(out_28[7]));
  register_8 register_8_3 (
    .D1(out_28[0]), .D2(out_28[1]), .D3(out_28[2]), .D4(out_28[3]), .D5(out_28[4]), .D6(out_28[5]),
    .D7(out_28[6]), .D8(out_28[7]), .LOAD(in_11), .CLK(CLK), .EN(in_12), .O1(register_8_3_o1[0]),
    .O2(register_8_3_o1[1]), .O3(register_8_3_o1[2]), .O4(register_8_3_o1[3]), .O5(register_8_3_o1[4]),
    .O6(register_8_3_o1[5]), .O7(register_8_3_o1[6]), .O8(register_8_3_o1[7]), .Q1(out_28[0]),
    .Q2(out_28[1]), .Q3(out_28[2]), .Q4(out_28[3]), .Q5(out_28[4]), .Q6(out_28[5]), .Q7(out_28[6]),
    .Q8(out_28[7]));
  register_8 register_8_4 (
    .D1(out_28[0]), .D2(out_28[1]), .D3(out_28[2]), .D4(out_28[3]), .D5(out_28[4]), .D6(out_28[5]),
    .D7(out_28[6]), .D8(out_28[7]), .LOAD(in_18), .CLK(CLK), .EN(in_19), .Q1(out_28[0]), .Q2(out_28[1]),
    .Q3(out_28[2]), .Q4(out_28[3]), .Q5(out_28[4]), .Q6(out_28[5]), .Q7(out_28[6]), .Q8(out_28[7]));  // open: O1, O2, O3, O4, O5, O6, O7, O8
  register_8 register_8_5 (
    .D1(out_28[0]), .D2(out_28[1]), .D3(out_28[2]), .D4(out_28[3]), .D5(out_28[4]), .D6(out_28[5]),
    .D7(out_28[6]), .D8(out_28[7]), .LOAD(in_24), .CLK(CLK), .EN(in_25), .Q1(out_28[0]), .Q2(out_28[1]),
    .Q3(out_28[2]), .Q4(out_28[3]), .Q5(out_28[4]), .Q6(out_28[5]), .Q7(out_28[6]), .Q8(out_28[7]));  // open: O1, O2, O3, O4, O5, O6, O7, O8
  register_8 register_8_6 (
    .D1(out_28[0]), .D2(out_28[1]), .D3(out_28[2]), .D4(out_28[3]), .D5(out_28[4]), .D6(out_28[5]),
    .D7(out_28[6]), .D8(out_28[7]), .LOAD(in_26), .CLK(CLK), .EN(in_27), .Q1(out_28[0]), .Q2(out_28[1]),
    .Q3(out_28[2]), .Q4(out_28[3]), .Q5(out_28[4]), .Q6(out_28[5]), .Q7(out_28[6]), .Q8(out_28[7]));  // open: O1, O2, O3, O4, O5, O6, O7, O8
  arithmetic_logic_unit arithmetic_logic_unit_1 (
    .A(register_8_2_o1), .B(register_8_3_o1), .ID(in_6), .OP(in_7), .SIGN(arithmetic_logic_unit_1_sign),
    .Q(out_28[7:0]), .Carry(arithmetic_logic_unit_1_carry));
  nor nor_1 (nor_1_out, out_28[0], out_28[1], out_28[2], out_28[3], out_28[4], out_28[5], out_28[6], out_28[7]);
  flags flags_1 (
    .Carry(arithmetic_logic_unit_1_carry), .Sign(arithmetic_logic_unit_1_sign), .Zero(nor_1_out),
    .LOAD(in_8), .CLK(CLK));  // open: Carry_out, Sign_out, Zero_out

  // Notes on the sheet:
  //   Random Access Memory
  //   Memory Address Register
  //   Memory Data Register
  //   Accumulator Register
  //   Temporary Register
  //   Register B
  //   Register C
  //   Instruction Register
endmodule
